# Fritzing sketch intval2 (saved by Fritzing 0.9.3b)
breadboards: 1

parts:
  12VDC = 2.1mm Barrel Jack with Terminal Block
  Trinket = Pro Trinket 5V
  S1 = H-Bridge with L298N
  Audio_Jack = Audio Jack (TRS) 3.5mm [package="PG203J [THT]"]
  DELAY = SWITCH-MOMENTARY-2 [package=tactile-switch-1101ne]
  SPEED = SWITCH-MOMENTARY-2 [package=tactile-switch-1101ne]
  DIR = SWITCH-MOMENTARY-2 [package=tactile-switch-1101ne]
  Microswitch = SWITCH-MOMENTARY-2 [package=tactile-switch-1101ne]
  Motor = DC Motor  # not connected
  LED1 = LEDs [package=led10mm]

nets:
  N1: 12VDC.POS, S1.12V
  GND: 12VDC.NEG, Trinket.GND, S1.GND, Audio_Jack.Tip, DELAY.1, SPEED.1, DIR.1, Microswitch.1, LED1.C
  N2: Trinket.VBAT, S1.5V
  N3: Trinket.D6, DIR.2
  N4: Trinket.D5, SPEED.2
  N5: Trinket.D4, DELAY.2
  N6: Trinket.D3, Audio_Jack.Ring
  N7: Trinket.D9, S1.IN3
  N8: Trinket.D10, S1.IN4
  N9: Trinket.D13, LED1.A
  N10: Trinket.A5, Microswitch.2
  N11: S1.ENA, S1.IN1, S1.IN2, S1.M1-02, S1.M2-01, S1.M2-02, S1.ENB-5V

custom parts:
  Pro Trinket 5V: The Pro Trinket 5V is like an Arduino Pro Mini with more pins and USB included. Built with the common core Arduino chip, the ATmega328p, it has 18 GPIO, 2 extra analog inputs, 28K of flash, and 2K of RAM. It has onboard USB bootloading support with Optiboot support, so you can either program your Pro Trinket over USB or with a FTDI cable. The Pro Trinket is programmable using the Arduino IDE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
  H-Bridge with L298N: h-bridge
